# Fritzing sketch QUT Motor Drive PCB (saved by Fritzing 0.9.3b)
circuit board: 6.1cm x 5.2cm
breadboards: 1

parts:
  C1 = Ceramic Capacitor [capacitance=100nF package="100 mil [THT, multilayer]"]
  C2 = Ceramic Capacitor [capacitance=100nF package="100 mil [THT, multilayer]"]
  Y1 = CRYSTAL [package=hc49u-v]
  C3 = Ceramic Capacitor [capacitance=100nF package="100 mil [THT, multilayer]"]
  C4 = Ceramic Capacitor [capacitance=100nF package="100 mil [THT, multilayer]"]
  R1 = Resistor [tolerance=±5% resistance=220 package=THT]
  S1 = Pushbutton [package="[THT]"]
  C5 = Ceramic Capacitor [capacitance=100nF package="100 mil [THT, multilayer]"]
  J1 = male pin header, 3 pins [form="♂ (male)"]
  J2 = male pin header, 3 pins [form="♂ (male)"]
  J3 = male pin header, 3 pins [form="♂ (male)"]
  J4 = male pin header, 3 pins [form="♂ (male)"]
  J5 = male pin header, 3 pins [form="♂ (male)"]
  J6 = male pin header, 3 pins [form="♂ (male)"]
  J7 = male pin header, 14 pins [form="♂ (male)"]
  J8 = male pin header, 14 pins [form="♂ (male)"]
  J9 = male pin header, 4 pins [form="♂ (male)"]
  J10 = male pin header, 4 pins [form="♂ (male)"]
  J11 = male pin header, 4 pins [form="♂ (male)"]
  R2 = Resistor [tolerance=±5% resistance=220 package=THT]
  Q1 = NPN-Transistor [package="TO92 [THT]"]
  R3 = Resistor [tolerance=±5% resistance=220 package=THT]
  Q2 = NPN-Transistor [package="TO92 [THT]"]
  R4 = Resistor [tolerance=±5% resistance=220 package=THT]
  Q3 = NPN-Transistor [package="TO92 [THT]"]
  Q4 = NPN-Transistor [package="TO92 [THT]"]
  R5 = Resistor [tolerance=±5% resistance=220 package=THT]
  R6 = Resistor [tolerance=±5% resistance=220 package=THT]
  J16 = CP2102 Serial Adaptor [form="♂ (male)" package=THT]
  U1 = atmega328 [package=dip]
  LED5 = LED - 3mm [color="Red (633nm)" package="3 mm [THT]"]
  LED4 = LED - 3mm [color="Red (633nm)" package="3 mm [THT]"]
  J17 = female pin header, 2 pins [form="♀ (female)"]
  LED2 = LED - 3mm [color="Red (633nm)" package="3 mm [THT]"]
  LED3 = LED - 3mm [color="Red (633nm)" package="3 mm [THT]"]
  LED1 = LED - 3mm [color="Red (633nm)" package="3 mm [THT]"]
  R7 = Resistor [tolerance=±5% resistance=220 package=THT]

nets:
  N1: C1.0, Y1.1, J8.pin6, U1.XLAT1
  GND: C1.1, C2.0, C3.0, S1.Pin_3, S1.Pin_4, C5.1, J1.pin3, J2.pin3, J3.pin3, J4.pin3, J5.pin3, J6.pin3, J7.pin7, J8.pin7, J9.pin1, J10.pin1, J11.pin1, Q1.E, Q2.E, R4.Pin_0, Q3.E, Q4.E, J16.GND, U1.GND, J17.pin2, R7.Pin_0
  N2: C2.1, Y1.2, J8.pin5, U1.XLAT2
  5V: C3.1, R1.Pin_1, C5.0, J7.pin9, J8.pin8, J9.pin2, J10.pin2, J11.pin2, J16.5v+, U1.VCC, U1.AVCC, LED5.anode, LED4.anode, LED2.anode, LED3.anode, LED1.anode
  N3: C4.0, R1.Pin_0, S1.Pin_1, S1.Pin_2, J8.pin14, U1.RESET
  DTR RESET: C4.1, J16.DTR
  N4: J1.pin1, J8.pin3, U1.D6_(PWM)
  6V: J1.pin2, J2.pin2, J3.pin2, J4.pin2, J5.pin2, J6.pin2, Q2.B, J17.pin1, R7.Pin_1
  N5: J2.pin1, J8.pin4, U1.D5_(PWM)
  N6: J3.pin1, J8.pin10, U1.D3_(PWM)
  N7: J4.pin1, J7.pin13, U1.D10_(PWM)
  N8: J5.pin1, J7.pin14, U1.D9_(PWM)
  N9: J6.pin1, J7.pin12, U1.D11_(PWM)
  I2C SCL: J7.pin1, J9.pin4, J10.pin4, J11.pin4, U1.A5
  N10: J7.pin2, J9.pin3, J10.pin3, J11.pin3, U1.A4
  N11: J7.pin3, U1.A3
  N12: J7.pin4, U1.A2
  N13: J7.pin5, U1.A1
  N14: J7.pin6, U1.A0
  N15: J7.pin8, U1.AREF
  D13: J7.pin10, Q1.B, U1.D13
  N16: J7.pin11, U1.D12
  N17: J8.pin1, U1.D8
  N18: J8.pin2, U1.D7
  N19: J8.pin9, U1.D4
  N20: J8.pin11, U1.D2
  Serial RX -> ARD TX: J8.pin12, Q3.B, J16.TXO, U1.D1_(TX)
  Serial TX -> ARD RX: J8.pin13, Q4.B, J16.RXI, U1.D0_(RX)
  N21: R2.Pin_0, Q1.C
  N22: R2.Pin_1, LED1.cathode
  N23: R3.Pin_0, Q2.C
  N24: R3.Pin_1, LED2.cathode
  N25: R4.Pin_1, LED3.cathode
  N26: Q3.C, R5.Pin_0
  N27: Q4.C, R6.Pin_0
  N28: R5.Pin_1, LED4.cathode
  N29: R6.Pin_1, LED5.cathode

notes:
  UTS ROBOSOC
  QUT MOTOR CTRL
